# Fritzing sketch circuit_diagram (saved by Fritzing 0.9.3b)

parts:
  J1 = Piezo Speaker
  Part1 = Adafruit HUZZAH32 ESP32 Feather [part_number="Adafruit #3405"]
  Part2 = Adafruit 2.4in TFT FeatherWing [part_number="Adafruit #3315"]
  Part3 = Adafruit AMG8833 8x8 GRID EYE
  BATT1 = LiPoly Battery (1300mAh)  # not connected
  U1 = SWITCH_SPDT [package=kps-1290]

nets:
  GND: J1.pin1, Part1.GND, Part2.GND, Part3.GND, U1.S
  N1: J1.pin2, Part1.IO21, Part2.G
  N2: Part1.IO17, Part2.TX
  N3: Part1.IO16, Part2.RX
  N4: Part1.MISO, Part2.MISO
  N5: Part1.MOSI, Part2.MOSI
  N6: Part1.SCK, Part2.SCLK
  N7: Part1.A5_IO4, Part2.F
  N8: Part1.A4_IO36, Part2.E
  N9: Part1.A3_I39, Part2.D
  N10: Part1.A2_I34, Part2.C
  N11: Part1.A1_DAC1, Part2.B
  N12: Part1.A0_DAC2, Part2.A
  N13: Part1.N/C, Part2.AREF
  3.3V: Part1.3.3V, Part2.3.3V, Part3.3.3V
  N14: Part1.RESET, Part2.!RESET
  N15: Part1.VBAT, Part2.VBAT
  N16: Part1.EN, Part2.EN, U1.P
  N17: Part1.VBUS, Part2.USB
  N18: Part1.IO13_A12, Part2.N
  N19: Part1.IO12_A11, Part2.M
  N20: Part1.IO27_A10, Part2.L
  N21: Part1.IO33_A9, Part2.K
  N22: Part1.IO15_A8, Part2.J
  N23: Part1.IO32_A7, Part2.I
  N24: Part1.IO14_A6, Part2.H
  N25: Part1.SCL, Part2.SCL, Part3.SCL
  N26: Part1.SDA, Part2.SDA, Part3.SDA

custom parts:
  Adafruit 2.4in TFT FeatherWing: Spice up your Feather project with a beautiful 2.4" touchscreen display shield with built in microSD card socket. This TFT display is 2.4" diagonal with a bright 4 white-LED backlight. You get 240x320 pixels with individual 16-bit color pixel control. It has way more resolution than a black and white 128x64 display. As a bonus, this display comes with a resistive touchscreen attached to it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
  LiPoly Battery (1300mAh): Lithium Ion Polymer Battery (1300mAh)
